# Fritzing sketch envduino (saved by Fritzing 0.8.0b)
breadboards: 2

parts:
  part = DHT22 Humidity and Temperature Sensor
  part_2 = BMP085 Breakout
  part_3 = Arduino Mega
  part_4 = Resistor [tolerance=±5% resistance=10k package=THT]
  LED1 = LED - 5mm [color="Yellow (592nm)" package="5 mm [THT]"]
  LED2 = LED - 5mm [color="Red (633nm)" package="5 mm [THT]"]
  LED4 = LED - 5mm [color="Green (560nm)" package="5 mm [THT]"]
  part_5 = Resistor [tolerance=±5% resistance=330 package=THT]
  part_6 = Resistor [tolerance=±5% resistance=330 package=THT]
  part_7 = Resistor [tolerance=±5% resistance=330 package=THT]

nets:
  VDD: part.VDD, part_3.+5V, part_4.Pin_1
  N1: part.DATA, part_3.D2, part_4.Pin_0
  GND: part.GND, part_3.GND, part_5.Pin_1, part_6.Pin_1, part_7.Pin_1
  N2: part_2.SCL, part_3.D21
  N3: part_2.SDA, part_3.D20
  N4: part_3.D22, LED4.cathode
  N5: part_3.D24, LED1.cathode
  N6: part_3.D26, LED2.cathode
  N7: LED1.anode, part_6.Pin_0
  N8: LED2.anode, part_5.Pin_0
  N9: LED4.anode, part_7.Pin_0

custom parts:
  BMP085 Breakout: A breakout for the BMP085 barometric pressure and temperature sensor
